// Logisim project alu.circ as structural Verilog: 3 circuits, main circuit subtractor
module subtractor (
  input  [7:0] in_1,
  input  [7:0] in_2,
  output [7:0] out_3,
  output out_4
);

  wire [7:0] not_1_out;

  assign not_1_out = ~in_2;  // NOT_Gate not_1, 8 bits wide
  Adder adder_1 (.a(in_1), .b(not_1_out), .out(out_3), .cin(1'b1), .cout(out_4));
endmodule

module main2 (
  input  [7:0] input_1,
  input  [7:0] input_2,
  input  [2:0] opcode,
  output [7:0] \output ,
  output SF,
  output ZF,
  output CF,
  output EQ,
  output OF
);

  wire adder_1_cout, and_2_out, and_3_out, and_4_out, and_5_out, and_6_out, and_7_out, comparator_1_gt,
       comparator_3_eq, comparator_4_eq, comparator_5_eq, comparator_6_eq, not_1_out, or_2_out, or_4_out,
       or_5_out, or_7_out, subtractor_1_out_4, xnor_1_out, xor_1_out, xor_2_out;
  wire [0:0] comparator_1_lt;
  wire [7:0] adder_1_out, and_1_out, or_1_out, shifter_1_out, shifter_2_out, shifter_3_out,
       subtractor_1_out_3;

  assign or_1_out = input_1 | input_2;  // OR_Gate or_1, 8 bits wide
  assign and_1_out = input_1 & input_2;  // AND_Gate and_1, 8 bits wide
  Comparator comparator_1 (.a(input_1), .b(input_2), .gt(comparator_1_gt), .eq(EQ), .lt(comparator_1_lt[0]));
  Adder adder_1 (.a(input_1), .b(input_2), .out(adder_1_out), .cin(1'b0), .cout(adder_1_cout));
  subtractor subtractor_1 (.in_1(input_1), .in_2(input_2), .out_4(subtractor_1_out_4), .out_3(subtractor_1_out_3));
  Shifter shifter_1 (.in(input_1), .\dist (input_2[7:5]), .out(shifter_1_out));
  Shifter #(.shift("lr")) shifter_2 (.in(input_1), .\dist (input_2[7:5]), .out(shifter_2_out));
  Shifter #(.shift("ar")) shifter_3 (.in(input_1), .\dist (input_2[7:5]), .out(shifter_3_out));
  Multiplexer #(.select(3), .width(8), .enable("false")) multiplexer_1 (
    .in0(or_1_out), .in1(and_1_out), .in2(adder_1_out), .in3(subtractor_1_out_3), .in4(shifter_1_out),
    .in5(shifter_2_out), .in6(shifter_3_out), .in7({{7{1'b0}}, comparator_1_lt[0]}), .out(\output ),
    .sel(opcode));
  xnor xnor_1 (xnor_1_out, input_2[7], input_1[7]);
  Comparator comparator_2 (.a(\output ), .b({8{1'b0}}), .eq(ZF));  // open: gt, lt
  Comparator #(.width(3)) comparator_3 (.a(opcode), .b(3'b010), .eq(comparator_3_eq));  // open: gt, lt
  Comparator #(.width(3)) comparator_4 (.a(opcode), .b(3'b011), .eq(comparator_4_eq));  // open: gt, lt
  Comparator #(.width(3)) comparator_5 (.a(opcode), .b(3'b110), .eq(comparator_5_eq));  // open: gt, lt
  and and_2 (and_2_out, xnor_1_out, SF);
  and and_3 (and_3_out, and_2_out, comparator_3_eq);
  xor xor_1 (xor_1_out, xnor_1_out, SF);
  and and_4 (and_4_out, comparator_4_eq, xor_1_out);
  or or_2 (or_2_out, and_3_out, and_4_out);
  or or_3 (OF, or_2_out, and_5_out);
  or or_4 (or_4_out, comparator_1_gt, comparator_4_eq);
  or or_5 (or_5_out, comparator_1_lt[0], comparator_3_eq);
  and and_5 (and_5_out, or_4_out, or_5_out, xor_2_out);
  xor xor_2 (xor_2_out, SF, CF);
  Comparator #(.width(1)) comparator_6 (.a(subtractor_1_out_4), .b(1'b1), .eq(comparator_6_eq));  // open: gt, lt
  not not_1 (not_1_out, comparator_6_eq);
  and and_6 (and_6_out, not_1_out, comparator_4_eq);
  or or_6 (CF, and_6_out, and_7_out);
  or or_7 (or_7_out, comparator_5_eq, comparator_4_eq, comparator_3_eq);
  and and_7 (and_7_out, adder_1_cout, comparator_3_eq);
  and and_8 (SF, or_7_out, \output [7]);

  // Notes on the sheet:
  //   addition
  //   subtraction
  //   signed shift
endmodule

module final_circuit (
  input  [2:0] opcode,
  input  [7:0] x,
  input  [7:0] result,
  input  [7:0] y,
  output SF,
  output ZF,
  output CF,
  output OF,
  output EQ
);

  main2 main2_1 (
    .input_1(x), .input_2(y), .\output (result), .EQ(EQ), .opcode(opcode), .ZF(ZF), .OF(OF), .CF(CF), .SF(SF));
endmodule
