// Logisim project part1.circ as structural Verilog: 4 circuits, main circuit main
module main (
  input  [3:0] X,
  input  [1:0] Y,
  input  CarryIn,
  output [3:0] Sum,
  output CarryOut
);

  wire [3:0] signext2to4__4out;

  signext2to4 signext2to4 (._2in(Y), ._4out(signext2to4__4out));
  fulladder4 fulladder4 (.x(X), .y(signext2to4__4out), .CarryIn(CarryIn), .Sum(Sum), .CarryOut(CarryOut));

  // Notes on the sheet:
  //   cs31 lab3, part 1
endmodule

module signext2to4 (
  input  [1:0] _2in,
  output [3:0] _4out
);


  assign _4out = {{3{_2in[1]}}, _2in[0]};
endmodule

module fulladder (
  input  CarryIn,
  input  x,
  input  y,
  output Sum,
  output CarryOut
);

  wire and_1_out, and_2_out, xor_1_out;

  xor xor_1 (xor_1_out, x, y);
  and and_1 (and_1_out, x, y);
  xor xor_2 (Sum, xor_1_out, CarryIn);
  and and_2 (and_2_out, xor_1_out, CarryIn);
  or or_1 (CarryOut, and_1_out, and_2_out);
endmodule

module fulladder4 (
  input  CarryIn,
  input  [3:0] x,
  input  [3:0] y,
  output [3:0] Sum,
  output CarryOut
);

  wire fulladder_1_carryout, fulladder_2_carryout, fulladder_3_carryout;

  fulladder fulladder_1 (.x(x[0]), .y(y[0]), .CarryIn(CarryIn), .CarryOut(fulladder_1_carryout), .Sum(Sum[0]));
  fulladder fulladder_2 (
    .x(x[1]), .y(y[1]), .CarryIn(fulladder_1_carryout), .CarryOut(fulladder_2_carryout), .Sum(Sum[1]));
  fulladder fulladder_3 (
    .x(x[2]), .y(y[2]), .CarryIn(fulladder_2_carryout), .CarryOut(fulladder_3_carryout), .Sum(Sum[2]));
  fulladder fulladder_4 (.x(x[3]), .y(y[3]), .CarryIn(fulladder_3_carryout), .CarryOut(CarryOut), .Sum(Sum[3]));
endmodule
